# Fritzing sketch Circuit (saved by Fritzing 0.9.6b)
circuit board: 25.0386cm x 18.614cm
breadboards: 1

parts:
  F1 = Arduino Uno (Rev3)
  F2 = Arduino Uno (Rev3)
  Power_Jack_7_5V_DC = Power Jack [package=power_jack_smd]
  Emergency_Stop = Square Pushbutton
  ON/OFF = SWITCH-SPST-2 [package=r_sw_th]
  Rotary_Encoder = KY-040 Rotary encoder [package="Breakout board"]
  Right_Servo2 = Basic Servo
  Right_Servo3 = Basic Servo
  stop_button = Pushbutton [package="[THT]"]
  Control_Display = LCD-16X2 [package=lcd-16x2_noholes]
  ihold_button = Pushbutton [package="[THT]"]
  R2_-_ihold2 = Resistor [tolerance=±5% resistance=47k package="0603 [SMD]"]
  R2_-_ihold3 = Resistor [tolerance=±5% resistance=47k package="0603 [SMD]"]
  4_7_uF1 = Capacitor Polarized [package=cpol-radial-10uf-25v]
  Alarms_Display = LCD-20x4 [package=lcd-20x4_noholes]
  Main = Arduino Uno (Rev3)
  R1 = Resistor [tolerance=±5% power=0.25 resistance=220 package=THT]
  R2 = Resistor [tolerance=±5% power=0.25 resistance=220 package=THT]
  R3 = Resistor [tolerance=±5% power=0.25 resistance=220 package=THT]
  Awake_Alarm = smd LED [color="Red (633nm)" package="1206 [SMD]"]
  PEEP_Alarm = smd LED [color="Red (633nm)" package="1206 [SMD]"]
  PIP_Alarm = smd LED [color="Red (633nm)" package="1206 [SMD]"]

nets:
  N1: F1.A4/SDA, Main.A4/SDA
  N2: F1.A5/SCL, Main.A5/SCL
  N3: F1.D9_PWM, Right_Servo2.pulse, Right_Servo3.pulse
  N4: F1.D13/SCK, F2.D13/SCK
  GND: F1.GND, F2.GND, Power_Jack_7_5V_DC.GND, Rotary_Encoder.GND, Right_Servo2.gnd, Right_Servo3.gnd, Control_Display.VSS, R2_-_ihold2.Pin_1, R2_-_ihold3.Pin_1, 4_7_uF1.-, Alarms_Display.VSS, Main.GND, R1.Pin_0, R2.Pin_0, R3.Pin_0
  N5: F1.D2, F2.D2
  5V: F1.5V, F2.5V, Rotary_Encoder.Vcc, stop_button.Pin_3, stop_button.Pin_4, Control_Display.VDD, ihold_button.Pin_3, ihold_button.Pin_4, 4_7_uF1.+, Alarms_Display.VDD, Alarms_Display.LED+, Main.5V
  VIN: F1.VIN, F2.VIN, ON/OFF.P, Right_Servo2.vcc, Right_Servo3.vcc, Main.VIN
  N6: F2.A3, Awake_Alarm.anode
  N7: F2.A4/SDA, PEEP_Alarm.anode
  N8: F2.A5/SCL, PIP_Alarm.anode
  N9: F2.D8, Alarms_Display.R_W
  N10: F2.D9_PWM, Alarms_Display.DB4
  N11: F2.D10_PWM/SS, Alarms_Display.DB5
  N12: F2.D11_PWM/MOSI, Alarms_Display.DB6
  N13: F2.D12/MISO, Alarms_Display.DB7
  N14: F2.D3_PWM, Alarms_Display.Red
  N15: F2.D4, ihold_button.Pin_1, ihold_button.Pin_2, R2_-_ihold3.Pin_0
  N16: F2.D7, Alarms_Display.RS
  N17: Power_Jack_7_5V_DC.GNDBREAK, Emergency_Stop.leg0
  N18: Emergency_Stop.leg1, ON/OFF.O
  N19: Rotary_Encoder.SW, Main.D7
  N20: Rotary_Encoder.DT, Main.D5_PWM
  N21: Rotary_Encoder.CLK, Main.D6_PWM
  N22: stop_button.Pin_1, stop_button.Pin_2, R2_-_ihold2.Pin_0, Main.D8
  N23: Control_Display.RX, Main.D11_PWM/MOSI
  N24: R1.Pin_1, Awake_Alarm.cathode
  N25: R2.Pin_1, PEEP_Alarm.cathode
  N26: R3.Pin_1, PIP_Alarm.cathode

notes:
  pins 17 and 18 are for green and blue backlight
  Pressure Sensor connections to F2
  Power to 5V
  GND to GND
  VO to A2

custom parts:
  KY-040 Rotary encoder: KY-040 Rotary Encoder with switch on breakout borad from AZ Delivery
  LCD-16X2: Standard text-only 16x2 parallel input LCD
  LCD-20x4: Standard text-only 20x4 parallel input LCD
